// Logisim project new_arc.circ as structural Verilog: 8 circuits, main circuit main
module main (
  output [7:0] out_1,
  output [7:0] out_2,
  output [7:0] out_3,
  output [7:0] out_4
);

  wire clock_1_out;
  wire [1:0] alu_and_regesters_1_out_8;
  wire [6:0] instruction_reg_1_out_4, instruction_reg_1_out_5;
  wire [7:0] alu_and_regesters_1_out_6, multiplexer_1_out, n8bit_counter_1_display, undriven;
  wire [8:0] instruction_reg_1_out_6;

  Clock clock_1 (.out(clock_1_out));
  instruction_reg instruction_reg_1 (
    .in_1(out_4), .clk(clock_1_out), .out_4(instruction_reg_1_out_4), .out_5(instruction_reg_1_out_5),
    .out_6(instruction_reg_1_out_6), .Flag_register(alu_and_regesters_1_out_8));
  _8bit_counter u_8bit_counter_1 (
    .count(clock_1_out), .inp_en(instruction_reg_1_out_6[3]), .in_4(out_4),
    .DISPLAY(n8bit_counter_1_display), .in_2(instruction_reg_1_out_6[2]));
  Multiplexer #(.select(2), .width(8), .enable("false")) multiplexer_1 (
    .in0(undriven), .in1(alu_and_regesters_1_out_6), .in2(out_4), .in3(n8bit_counter_1_display),
    .out(multiplexer_1_out), .sel(instruction_reg_1_out_6[1:0]));
  alu_and_regesters alu_and_regesters_1 (
    .in_1(instruction_reg_1_out_4), .in_2(instruction_reg_1_out_5), .in_4(clock_1_out), .out_7(out_1),
    .out_9(out_2), .out_10(out_3), .in_3(out_4), .out_6(alu_and_regesters_1_out_6),
    .out_8(alu_and_regesters_1_out_8), .in_5(instruction_reg_1_out_6[6]));
  RAM #(.bus("separate")) ram_1 (
    .addr(multiplexer_1_out), .din(out_4), .data(out_4), .str(instruction_reg_1_out_6[5]), .sel(1'b1),
    .clk(clock_1_out), .ld(instruction_reg_1_out_6[4]));  // open: clr
endmodule

module _8bit_reg (
  input  [7:0] in_1,
  input  [7:0] in_2,
  input  clk,
  input  select,
  input  out_enable,
  input  _0___data_bus,
  output [7:0] out_7,
  output [7:0] out_8
);

  wire and_1_out;
  wire [7:0] multiplexer_1_out;

  and and_1 (and_1_out, clk, select);
  Multiplexer #(.width(8), .enable("false")) multiplexer_1 (
    .in0(in_1), .in1(in_2), .out(multiplexer_1_out), .sel(_0___data_bus));
  D_Flip_Flop #(.trigger("falling")) d_ff_1 (
    .clk(and_1_out), .D(multiplexer_1_out[0]), .Q(out_7[0]));  // open: Qn, preset, en, reset
  D_Flip_Flop #(.trigger("falling")) d_ff_2 (
    .clk(and_1_out), .D(multiplexer_1_out[1]), .Q(out_7[1]));  // open: Qn, preset, en, reset
  D_Flip_Flop #(.trigger("falling")) d_ff_3 (
    .clk(and_1_out), .D(multiplexer_1_out[2]), .Q(out_7[2]));  // open: Qn, preset, en, reset
  D_Flip_Flop #(.trigger("falling")) d_ff_4 (
    .clk(and_1_out), .D(multiplexer_1_out[3]), .Q(out_7[3]));  // open: Qn, preset, en, reset
  D_Flip_Flop #(.trigger("falling")) d_ff_5 (
    .clk(and_1_out), .D(multiplexer_1_out[4]), .Q(out_7[4]));  // open: Qn, preset, en, reset
  D_Flip_Flop #(.trigger("falling")) d_ff_6 (
    .clk(and_1_out), .D(multiplexer_1_out[5]), .Q(out_7[5]));  // open: Qn, preset, en, reset
  D_Flip_Flop #(.trigger("falling")) d_ff_7 (
    .clk(and_1_out), .D(multiplexer_1_out[6]), .Q(out_7[6]));  // open: Qn, preset, en, reset
  D_Flip_Flop #(.trigger("falling")) d_ff_8 (
    .clk(and_1_out), .D(multiplexer_1_out[7]), .Q(out_7[7]));  // open: Qn, preset, en, reset
  assign out_8 = out_enable ? out_7 : 8'bz;  // Controlled_Buffer controlled_buffer_1

  // Notes on the sheet:
  //   data bus
  //   alu
  //   1 -> ALU
endmodule

module ALU (
  input  [7:0] in_1,
  input  [6:0] in_2,
  input  [7:0] in_3,
  input  in_4,
  output [7:0] out_5,
  output [7:0] out_6,
  output [1:0] out_7
);

  wire adder_1_cout, nor_1_out;
  wire [7:0] adder_1_out, and_1_out, controled_inv_1_out_3, controled_inv_2_out_3, multiplexer_1_out,
       multiplexer_2_out, multiplexer_3_out;

  Multiplexer #(.width(8), .enable("false")) multiplexer_1 (
    .in0(in_1), .in1({8{1'b0}}), .out(multiplexer_1_out), .sel(in_2[0]));
  controled_inv controled_inv_1 (.in_1(multiplexer_1_out), .in_2(in_2[1]), .out_3(controled_inv_1_out_3));
  Multiplexer #(.width(8), .enable("false")) multiplexer_2 (
    .in0(in_3), .in1({8{1'b0}}), .out(multiplexer_2_out), .sel(in_2[2]));
  controled_inv controled_inv_2 (.in_1(multiplexer_2_out), .in_2(in_2[3]), .out_3(controled_inv_2_out_3));
  Adder adder_1 (
    .a(controled_inv_1_out_3), .b(controled_inv_2_out_3), .out(adder_1_out), .cout(adder_1_cout));  // open: cin
  assign and_1_out = controled_inv_1_out_3 & controled_inv_2_out_3;  // AND_Gate and_1, 8 bits wide
  Multiplexer #(.width(8), .enable("false")) multiplexer_3 (
    .in0(adder_1_out), .in1(and_1_out), .out(multiplexer_3_out), .sel(in_2[5]));
  controled_inv controled_inv_3 (.in_1(multiplexer_3_out), .in_2(in_2[4]), .out_3(out_5));
  assign out_6 = in_2[6] ? out_5 : 8'bz;  // Controlled_Buffer controlled_buffer_1
  nor nor_1 (nor_1_out, out_5[0], out_5[1], out_5[2], out_5[3], out_5[4], out_5[5], out_5[6], out_5[7]);
  D_Flip_Flop #(.trigger("falling")) d_ff_1 (.clk(in_4), .D(nor_1_out), .Q(out_7[0]));  // open: Qn, preset, en, reset
  D_Flip_Flop #(.trigger("falling")) d_ff_2 (
    .clk(in_4), .D(adder_1_cout), .Q(out_7[1]));  // open: Qn, preset, en, reset

  // Notes on the sheet:
  //   X
  //   Z x
  //   INV X
  //   Y
  //   Z y
  //   INV Y
  //   INV out
  //   X+Y||X&Y
  //   0           1
endmodule

module controled_inv (
  input  [7:0] in_1,
  input  in_2,
  output [7:0] out_3
);

  xor xor_1 (out_3[0], in_1[0], in_2);
  xor xor_2 (out_3[1], in_1[1], in_2);
  xor xor_3 (out_3[2], in_1[2], in_2);
  xor xor_4 (out_3[3], in_1[3], in_2);
  xor xor_5 (out_3[4], in_1[4], in_2);
  xor xor_6 (out_3[5], in_1[5], in_2);
  xor xor_7 (out_3[6], in_1[6], in_2);
  xor xor_8 (out_3[7], in_1[7], in_2);
endmodule

module _8bit_counter (
  input  count,
  input  in_2,
  input  inp_en,
  input  [7:0] in_4,
  output [7:0] DISPLAY
);

  wire and_1_out, and_2_out, d_ff_1_qn, d_ff_2_qn, d_ff_3_qn, d_ff_4_qn, d_ff_5_qn, d_ff_6_qn, d_ff_7_qn,
       d_ff_8_qn, multiplexer_1_out, multiplexer_2_out, multiplexer_3_out, multiplexer_4_out,
       multiplexer_5_out, multiplexer_6_out, multiplexer_7_out, multiplexer_8_out, multiplexer_9_out,
       multiplexer_10_out, multiplexer_11_out, multiplexer_12_out, multiplexer_13_out, multiplexer_14_out,
       multiplexer_15_out, multiplexer_16_out;

  and and_1 (and_1_out, count, in_2);
  and and_2 (and_2_out, in_2, inp_en);
  Multiplexer #(.enable("false")) multiplexer_1 (
    .in0(and_1_out), .in1(and_1_out), .out(multiplexer_1_out), .sel(and_2_out));
  Multiplexer #(.enable("false")) multiplexer_2 (
    .in0(d_ff_1_qn), .in1(in_4[0]), .out(multiplexer_2_out), .sel(and_2_out));
  Multiplexer #(.enable("false")) multiplexer_3 (
    .in0(DISPLAY[0]), .in1(and_1_out), .out(multiplexer_3_out), .sel(and_2_out));
  Multiplexer #(.enable("false")) multiplexer_4 (
    .in0(d_ff_2_qn), .in1(in_4[1]), .out(multiplexer_4_out), .sel(and_2_out));
  Multiplexer #(.enable("false")) multiplexer_5 (
    .in0(DISPLAY[1]), .in1(and_1_out), .out(multiplexer_5_out), .sel(and_2_out));
  Multiplexer #(.enable("false")) multiplexer_6 (
    .in0(d_ff_3_qn), .in1(in_4[2]), .out(multiplexer_6_out), .sel(and_2_out));
  Multiplexer #(.enable("false")) multiplexer_7 (
    .in0(DISPLAY[2]), .in1(and_1_out), .out(multiplexer_7_out), .sel(and_2_out));
  Multiplexer #(.enable("false")) multiplexer_8 (
    .in0(d_ff_4_qn), .in1(in_4[3]), .out(multiplexer_8_out), .sel(and_2_out));
  Multiplexer #(.enable("false")) multiplexer_9 (
    .in0(DISPLAY[3]), .in1(and_1_out), .out(multiplexer_9_out), .sel(and_2_out));
  Multiplexer #(.enable("false")) multiplexer_10 (
    .in0(d_ff_5_qn), .in1(in_4[4]), .out(multiplexer_10_out), .sel(and_2_out));
  Multiplexer #(.enable("false")) multiplexer_11 (
    .in0(DISPLAY[4]), .in1(and_1_out), .out(multiplexer_11_out), .sel(and_2_out));
  Multiplexer #(.enable("false")) multiplexer_12 (
    .in0(d_ff_6_qn), .in1(in_4[5]), .out(multiplexer_12_out), .sel(and_2_out));
  Multiplexer #(.enable("false")) multiplexer_13 (
    .in0(DISPLAY[5]), .in1(and_1_out), .out(multiplexer_13_out), .sel(and_2_out));
  Multiplexer #(.enable("false")) multiplexer_14 (
    .in0(d_ff_7_qn), .in1(in_4[6]), .out(multiplexer_14_out), .sel(and_2_out));
  Multiplexer #(.enable("false")) multiplexer_15 (
    .in0(DISPLAY[6]), .in1(and_1_out), .out(multiplexer_15_out), .sel(and_2_out));
  Multiplexer #(.enable("false")) multiplexer_16 (
    .in0(d_ff_8_qn), .in1(in_4[7]), .out(multiplexer_16_out), .sel(and_2_out));
  D_Flip_Flop #(.trigger("falling")) d_ff_1 (
    .clk(multiplexer_1_out), .D(multiplexer_2_out), .Q(DISPLAY[0]), .Qn(d_ff_1_qn));  // open: preset, en, reset
  D_Flip_Flop #(.trigger("falling")) d_ff_2 (
    .clk(multiplexer_3_out), .D(multiplexer_4_out), .Q(DISPLAY[1]), .Qn(d_ff_2_qn));  // open: preset, en, reset
  D_Flip_Flop #(.trigger("falling")) d_ff_3 (
    .clk(multiplexer_5_out), .D(multiplexer_6_out), .Q(DISPLAY[2]), .Qn(d_ff_3_qn));  // open: preset, en, reset
  D_Flip_Flop #(.trigger("falling")) d_ff_4 (
    .clk(multiplexer_7_out), .D(multiplexer_8_out), .Q(DISPLAY[3]), .Qn(d_ff_4_qn));  // open: preset, en, reset
  D_Flip_Flop #(.trigger("falling")) d_ff_5 (
    .clk(multiplexer_9_out), .D(multiplexer_10_out), .Q(DISPLAY[4]), .Qn(d_ff_5_qn));  // open: preset, en, reset
  D_Flip_Flop #(.trigger("falling")) d_ff_6 (
    .clk(multiplexer_11_out), .D(multiplexer_12_out), .Q(DISPLAY[5]), .Qn(d_ff_6_qn));  // open: preset, en, reset
  D_Flip_Flop #(.trigger("falling")) d_ff_7 (
    .clk(multiplexer_13_out), .D(multiplexer_14_out), .Q(DISPLAY[6]), .Qn(d_ff_7_qn));  // open: preset, en, reset
  D_Flip_Flop #(.trigger("falling")) d_ff_8 (
    .clk(multiplexer_15_out), .D(multiplexer_16_out), .Q(DISPLAY[7]), .Qn(d_ff_8_qn));  // open: preset, en, reset
endmodule

module _3bit_counter (
  input  in_1,
  input  in_2,
  output out_3,
  output out_4,
  output out_5
);

  wire d_ff_1_q, d_ff_2_qn, d_ff_3_qn, d_ff_4_qn, not_1_out;

  D_Flip_Flop #(.trigger("falling")) d_ff_1 (
    .clk(in_1), .D(in_2), .Q(d_ff_1_q), .reset(not_1_out));  // open: Qn, preset, en
  not not_1 (not_1_out, in_2);
  D_Flip_Flop #(.trigger("falling")) d_ff_2 (
    .clk(in_1), .D(d_ff_2_qn), .Q(out_3), .Qn(d_ff_2_qn), .reset(d_ff_1_q));  // open: preset, en
  D_Flip_Flop #(.trigger("falling")) d_ff_3 (
    .clk(out_3), .D(d_ff_3_qn), .Q(out_4), .Qn(d_ff_3_qn), .reset(d_ff_1_q));  // open: preset, en
  D_Flip_Flop #(.trigger("falling")) d_ff_4 (
    .clk(out_4), .D(d_ff_4_qn), .Q(out_5), .Qn(d_ff_4_qn), .reset(d_ff_1_q));  // open: preset, en
endmodule

module instruction_reg (
  input  [7:0] in_1,
  input  clk,
  input  [1:0] Flag_register,
  output [6:0] out_4,
  output [6:0] out_5,
  output [8:0] out_6
);

  wire nor_1_out;
  wire [7:0] n8bit_reg_1_out_7;
  wire [12:10] n3bit_counter_1_out_3;
  wire [23:23] rom_1_data;

  _3bit_counter u_3bit_counter_1 (
    .in_1(clk), .out_3(n3bit_counter_1_out_3[10]), .out_4(n3bit_counter_1_out_3[11]), .in_2(rom_1_data[23]),
    .out_5(n3bit_counter_1_out_3[12]));
  nor nor_1 (nor_1_out, n3bit_counter_1_out_3[10], n3bit_counter_1_out_3[11], n3bit_counter_1_out_3[12]);
  _8bit_reg u_8bit_reg_1 (
    .clk(nor_1_out), .select(nor_1_out), .out_7(n8bit_reg_1_out_7), .in_1(in_1), ._0___data_bus(1'b0));  // open: out_8, out_enable, in_2
  ROM #(.addrWidth(13), .dataWidth(24)) rom_1 (
    .addr({n3bit_counter_1_out_3, n8bit_reg_1_out_7, Flag_register[0], Flag_register[1]}),
    .data({rom_1_data[23], out_6, out_5, out_4}), .sel(1'b1));

  // Notes on the sheet:
  //   data bus
  //   contents of rom_1 (hex, n*v repeats v):
  //   1024*5c000 4*850080 4*850400 4*851000
  //   ALU controll
  //   Register controll
  //   Ram IP SP controll
endmodule

module alu_and_regesters (
  input  [6:0] in_1,
  input  [6:0] in_2,
  input  [7:0] in_3,
  input  in_4,
  input  in_5,
  output [7:0] out_6,
  output [7:0] out_7,
  output [1:0] out_8,
  output [7:0] out_9,
  output [7:0] out_10
);

  _8bit_reg u_8bit_reg_1 (
    .clk(in_4), .select(in_2[0]), .out_8(in_3), .out_enable(in_2[1]), .out_7(out_7), .in_1(in_3),
    .in_2(out_6), ._0___data_bus(in_2[2]));
  _8bit_reg u_8bit_reg_2 (
    .clk(in_4), .select(in_2[3]), .out_8(in_3), .out_enable(in_2[4]), .out_7(out_9), .in_1(in_3),
    ._0___data_bus(1'b0));  // open: in_2
  _8bit_reg u_8bit_reg_3 (
    .clk(in_4), .select(in_2[5]), .out_8(in_3), .out_enable(in_2[6]), .out_7(out_10), .in_1(in_3),
    ._0___data_bus(1'b0));  // open: in_2
  ALU alu_1 (.in_1(out_7), .in_3(in_3), .out_6(in_3), .in_2(in_1), .out_5(out_6), .in_4(in_5), .out_7(out_8));
endmodule
